# Fritzing sketch schemat (saved by Fritzing 0.9.3b)
breadboards: 1

parts:
  Mod1 = Raspberry Pi 4B
  Part2 = Logic Level Converter
  Part3 = Triple Axis Accelerometer Breakout - ADXL345
  R1 = Resistor [tolerance=±5% resistance=6.8k package=THT]
  R2 = Resistor [tolerance=±5% resistance=6.8k package=THT]

nets:
  N1: Mod1.3V3, Part2.LV
  5V: Mod1.5V, Part2.HV, Part3.VCC, R1.Pin_1, R2.Pin_1
  N2: Mod1.GPIO2, Part2.TX_LV
  N3: Mod1.GPIO3, Part2.RX_LV
  GND: Mod1.GND, Part2.GND, Part3.GND
  N4: Part2.TX_HV, Part3.SDA, R2.Pin_0
  N5: Part2.RX_HV, Part3.SCL, R1.Pin_0
